# Fritzing sketch Fritzing_Prototype (saved by Fritzing 0.9.1b)
breadboards: 1

parts:
  R1 = Resistor [tolerance=±5% resistance=1k package=THT]
  R2 = Resistor [tolerance=±5% resistance=21 package=THT]
  Onderdeel1 = Arduino Uno (Rev3)
  S1 = Round Pushbutton
  LED1 = LED - 5mm [color="Yellow (595nm)" package="5 mm [THT]"]
  RFID1 = RFID Reader

nets:
  N1: R1.Pin_0, Onderdeel1.D13/SCK, S1.leg1
  N2: R1.Pin_1, Onderdeel1.GND, S1.leg0, LED1.cathode, RFID1.CP
  N3: R2.Pin_0, LED1.anode
  N4: R2.Pin_1, Onderdeel1.D11_PWM/MOSI
  N5: Onderdeel1.D8, RFID1.ANT1
  N6: Onderdeel1.D6_PWM, RFID1.ANT0
  N7: Onderdeel1.5V, RFID1.RES
